# Fritzing sketch Sketch_projetoArduino (saved by Fritzing 0.9.3b)
breadboards: 4

parts:
  Componente1 = Arduino Uno (Rev3) - ICSP
  LED3 = RGB LED (com. cathode, rgb) [package="5 mm [THT]"]
  LED4 = RGB LED (com. cathode, rgb) [package="5 mm [THT]"]
  LED5 = RGB LED (com. cathode, rgb) [package="5 mm [THT]"]
  LED6 = RGB LED (com. cathode, rgb) [package="5 mm [THT]"]
  LED7 = RGB LED (com. cathode, rgb) [package="5 mm [THT]"]
  R1 = Resistor [tolerance=±5% resistance=220 package="2512 [SMD]"]
  R2 = Resistor [tolerance=±5% resistance=220 package="2512 [SMD]"]
  R3 = Resistor [tolerance=±5% resistance=220 package="2512 [SMD]"]
  R4 = Resistor [tolerance=±5% resistance=220 package="2512 [SMD]"]
  R5 = Resistor [tolerance=±5% resistance=220 package="2512 [SMD]"]
  R6 = Resistor [tolerance=±5% resistance=220 package="2512 [SMD]"]
  U2 = 74HC595 [package="DIP16 [THT]"]
  U3 = 74HC595 [package="DIP16 [THT]"]
  LED8 = RGB LED (com. cathode, rgb) [package="5 mm [THT]"]
  U4 = 74HC595 [package="DIP16 [THT]"]
  S1 = Pushbutton [package="[THT]"]

nets:
  N1: Componente1.D8, U4.ST_CP
  N2: Componente1.D9_PWM, U4.SH_CP
  N3: Componente1.D2, Componente1.GND, R1.Pin_1, R2.Pin_1, R4.Pin_1, R5.Pin_1, R6.Pin_1, S1.Pin_1, S1.Pin_2
  N4: Componente1.D3_PWM, U2.DS
  N5: Componente1.D4, U2.SH_CP
  N6: Componente1.D5_PWM, U2.ST_CP
  N7: Componente1.D6_PWM, U3.SH_CP
  N8: Componente1.D7, U3.ST_CP
  N9: LED3.red_anode, U2.Q1
  N10: LED3.common_cathode, R2.Pin_0
  N11: LED3.green_anode, U3.Q1
  N12: LED3.blue_anode, U4.Q1
  N13: LED4.red_anode, U2.Q3
  N14: LED4.common_cathode, R4.Pin_0
  N15: LED4.green_anode, U3.Q3
  N16: LED4.blue_anode, U4.Q3
  N17: LED5.red_anode, U2.Q2
  N18: LED5.common_cathode, R3.Pin_0
  N19: LED5.green_anode, U3.Q2
  N20: LED6.red_anode, U2.Q5
  N21: LED6.common_cathode, R6.Pin_0
  N22: LED6.green_anode, U3.Q5
  N23: LED6.blue_anode, U4.Q5
  N24: LED7.red_anode, U2.Q4
  N25: LED7.common_cathode, R5.Pin_0
  N26: LED7.green_anode, U3.Q4
  N27: LED7.blue_anode, U4.Q4
  N28: R1.Pin_0, LED8.common_cathode
  N29: U2.Q6, U3.DS
  N30: U2.Q0, LED8.red_anode
  N31: U3.Q6, U4.DS
  N32: U3.Q0, LED8.green_anode
  N33: LED8.blue_anode, U4.Q0
  N34: S1.Pin_3, S1.Pin_4
